# Fritzing sketch Sketch (saved by Fritzing 0.9.3b)
breadboards: 1

parts:
  Q2 = Basic FET N-Channel [package="D2Pak [SMD]"]
  U1 = attiny85 [package=dip]
  220_Ohm_Resistor = Resistor [tolerance=±5% resistance=220 package=THT]
  220_Ohm_Resistor1 = Resistor [tolerance=±5% resistance=100 package=THT]
  VCC1 = 4 x AAA Battery Mount
  Bauteil1 = Arduino Uno (Rev3)
  Bauteil3 = Arduino Cellular Shield
  ADC_HX712 = HX711 Weighing Sensor Module
  LOAD_CELL = IC, DIP package, 4 pins [chip_label="Load Cell"]

nets:
  N1: Q2.Gate, 220_Ohm_Resistor.Pin_1
  GND: Q2.drain, Bauteil1.GND, Bauteil3.GND, ADC_HX712.E-
  N2: Q2.source, U1.Pin_4, 220_Ohm_Resistor1.Pin_0, VCC1.-
  N3: U1.Pin_5, 220_Ohm_Resistor.Pin_0, 220_Ohm_Resistor1.Pin_1
  5V: U1.Pin_8, VCC1.+, Bauteil1.5V, Bauteil3.5V, ADC_HX712.E+
  N4: Bauteil1.D9_PWM, Bauteil3.A2
  N5: Bauteil1.D5_PWM, ADC_HX712.A+
  N6: Bauteil1.D6_PWM, ADC_HX712.A-
  N7: ADC_HX712.VCC, LOAD_CELL.pin3
  N8: ADC_HX712.GND, LOAD_CELL.pin1
  N9: ADC_HX712.DO/RX, LOAD_CELL.pin2
  N10: ADC_HX712.CK/TX, LOAD_CELL.pin4
